// Logisim project cpu.circ as structural Verilog: 1 circuit, main circuit cpu
module cpu (
  input  clk,
  input  [31:0] INSTRUCTION,
  input  [31:0] READ_DATA,
  output [31:0] WRITE_ADDRESS,
  output [31:0] PROGRAM_COUNTER,
  output [31:0] ra,
  output [31:0] sp,
  output [31:0] t0,
  output [31:0] t1,
  output [31:0] t2,
  output [31:0] s0,
  output [31:0] s1,
  output [31:0] a0,
  output [31:0] tohost,
  output [3:0] WRITE_ENABLE,
  output [31:0] WRITE_DATA
);

  wire ASel, BrEq, BrLt, BrUn, BSel, CSRSel, CSRWen, MemRW, PCSel, RegWEn;
  wire [1:0] bit_extender_4_out, demultiplexer_2_out0, demultiplexer_2_out1, WBSel;
  wire [2:0] funct3, ImmSel;
  wire [3:0] ALUSel, bit_extender_5_out, demultiplexer_1_out0;
  wire [7:0] b0, b1, multiplexer_6_out;
  wire [15:0] multiplexer_7_out;
  wire [31:0] adder_1_out, adder_2_out, bit_extender_1_out, bit_extender_2_out, bit_extender_3_out, CSRin,
       imm0, inst, multiplexer_1_out, multiplexer_2_out, multiplexer_4_out, multiplexer_5_out, pc, reg1, wb,
       wb_rdata;
  wire [31:16] reg2;

  Adder #(.width(32)) adder_1 (.a(PROGRAM_COUNTER), .b(32'h4), .out(adder_1_out));  // open: cin, cout
  Multiplexer #(.width(32)) multiplexer_1 (
    .in0(adder_1_out), .in1(WRITE_ADDRESS), .out(multiplexer_1_out), .sel(PCSel));
  Register #(.width(32)) u_PC (.D(multiplexer_1_out), .en(1'b1), .clk(clk), .Q(PROGRAM_COUNTER));  // open: clr
  control_logic control_logic_1 (
    .inst({inst[31:15], funct3, inst[11:0]}), .BrEq(BrEq), .BrLt(BrLt), .CSRWen(CSRWen), .PCSel(PCSel),
    .RegWEn(RegWEn), .ImmSel(ImmSel), .BrUn(BrUn), .ASel(ASel), .BSel(BSel), .ALUSel(ALUSel), .MemRW(MemRW),
    .WBSel(WBSel), .CSRSel(CSRSel));
  Register #(.width(32)) register_1 (.D(PROGRAM_COUNTER), .en(1'b1), .clk(clk), .Q(pc));  // open: clr
  Multiplexer #(.width(32)) multiplexer_2 (.in0(INSTRUCTION), .in1(32'h33), .out(multiplexer_2_out), .sel(PCSel));
  Register #(.width(32)) register_2 (
    .D(multiplexer_2_out), .en(1'b1), .clk(clk), .Q({inst[31:15], funct3, inst[11:0]}));  // open: clr
  regfile regfile_1 (
    .rs1(inst[19:15]), .rs2(inst[24:20]), .rd(inst[11:7]), .Write_Data(wb), .RegWEn(RegWEn), .clk(clk),
    .ra(ra), .sp(sp), .t0(t0), .t1(t1), .t2(t2), .s0(s0), .s1(s1), .a0(a0), .Read_Data_1(reg1),
    .Read_Data_2({reg2, b1, b0}));
  imm_gen imm_gen_1 (.inst({inst[31:15], funct3, inst[11:0]}), .ImmSel(ImmSel), .imm(imm0));
  Multiplexer #(.width(32)) multiplexer_3 (.in0(reg1), .in1(bit_extender_1_out), .out(CSRin), .sel(CSRSel));
  assign bit_extender_1_out = {{27{1'b0}}, inst[19:15]};  // Bit_Extender bit_extender_1
  Multiplexer #(.width(32)) multiplexer_4 (.in0(reg1), .in1(pc), .out(multiplexer_4_out), .sel(ASel));
  Multiplexer #(.width(32)) multiplexer_5 (.in0({reg2, b1, b0}), .in1(imm0), .out(multiplexer_5_out), .sel(BSel));
  alu alu_1 (.A(multiplexer_4_out), .B(multiplexer_5_out), .ALUSel(ALUSel), .Result(WRITE_ADDRESS));
  branch_comp branch_comp_1 (.rs1(reg1), .rs2({reg2, b1, b0}), .BrUn(BrUn), .BrEq(BrEq), .BrLt(BrLt));
  csr csr_1 (.CSR_address(inst[31:20]), .CSR_din(CSRin), .CSR_WE(CSRWen), .clk(clk), .tohost(tohost));
  Adder #(.width(32)) adder_2 (.a(pc), .b(32'h4), .out(adder_2_out));  // open: cin, cout
  Multiplexer #(.select(2), .width(8)) multiplexer_6 (
    .in0(READ_DATA[7:0]), .in1(READ_DATA[15:8]), .in2(READ_DATA[23:16]), .in3(READ_DATA[31:24]),
    .out(multiplexer_6_out), .sel(WRITE_ADDRESS[1:0]));
  Multiplexer #(.width(16)) multiplexer_7 (
    .in0(READ_DATA[15:0]), .in1(READ_DATA[31:16]), .out(multiplexer_7_out), .sel(WRITE_ADDRESS[1]));
  Multiplexer #(.select(2), .width(32)) multiplexer_8 (
    .in0(WRITE_ADDRESS), .in1(wb_rdata), .in2(adder_2_out), .in3(adder_2_out), .out(wb), .sel(WBSel));
  assign bit_extender_2_out = {{24{multiplexer_6_out[7]}}, multiplexer_6_out};  // Bit_Extender bit_extender_2
  assign bit_extender_3_out = {{16{multiplexer_7_out[15]}}, multiplexer_7_out};  // Bit_Extender bit_extender_3
  Multiplexer #(.select(2), .width(32)) multiplexer_9 (
    .in0(bit_extender_2_out), .in1(bit_extender_3_out), .in2(READ_DATA), .out(wb_rdata), .sel(funct3[1:0]));  // open: in3
  assign bit_extender_4_out = {{1{MemRW}}, MemRW};  // Bit_Extender bit_extender_4
  assign bit_extender_5_out = {{3{MemRW}}, MemRW};  // Bit_Extender bit_extender_5
  Demultiplexer #(.select(2)) demultiplexer_1 (
    .out0(demultiplexer_1_out0[0]), .out1(demultiplexer_1_out0[1]), .out2(demultiplexer_1_out0[2]),
    .out3(demultiplexer_1_out0[3]), .in(MemRW), .sel(WRITE_ADDRESS[1:0]));
  Demultiplexer #(.width(2)) demultiplexer_2 (
    .out0(demultiplexer_2_out0), .out1(demultiplexer_2_out1), .in(bit_extender_4_out), .sel(WRITE_ADDRESS[1]));
  Multiplexer #(.select(2), .width(32)) multiplexer_10 (
    .in0({b0, b0, b0, b0}), .in1({b1, b0, b1, b0}), .in2({reg2, b1, b0}), .out(WRITE_DATA), .sel(funct3[1:0]));  // open: in3
  Multiplexer #(.select(2), .width(4)) multiplexer_11 (
    .in0(demultiplexer_1_out0), .in1({demultiplexer_2_out1, demultiplexer_2_out0}), .in2(bit_extender_5_out),
    .out(WRITE_ENABLE), .sel(funct3[1:0]));  // open: in3

  // Other names for the same wires on the sheet: alu_res[31:0] = WRITE_ADDRESS; wa0[1:0] = WRITE_ADDRESS[1:0];
  //   wa1 = WRITE_ADDRESS[1]; opcode[6:0] = inst[6:0]; rd[4:0] = inst[11:7]; inst[14:12] = funct3;
  //   rs1[4:0] = inst[19:15]; rs2[4:0] = inst[24:20]; reg2[15:0] = {b1, b0}

  // Notes on the sheet:
  //   Output to IMEM
  //   Inputs from IMEM
  //   Outputs To DMEM
  //   Inputs From DMEM
endmodule
